// Digital circuit add_sub_16_bits.dig as structural Verilog
module add_sub_16_bits (
  input  Sub,
  input  [15:0] A,
  input  [15:0] B,
  output [15:0] Sum,
  output Cout,
  output SF,
  output ZF,
  output OF
);

  wire xor_1_out, xor_2_out, xor_3_out, xor_4_out, xor_5_out, xor_6_out, xor_7_out, xor_8_out, xor_9_out,
       xor_10_out, xor_11_out, xor_12_out, xor_13_out, xor_14_out, xor_15_out, xor_16_out;

  xor xor_1 (xor_1_out, Sub, B[0]);
  xor xor_2 (xor_2_out, Sub, B[1]);
  xor xor_3 (xor_3_out, Sub, B[2]);
  xor xor_4 (xor_4_out, Sub, B[3]);
  xor xor_5 (xor_5_out, Sub, B[4]);
  xor xor_6 (xor_6_out, Sub, B[5]);
  xor xor_7 (xor_7_out, Sub, B[6]);
  xor xor_8 (xor_8_out, Sub, B[7]);
  xor xor_9 (xor_9_out, Sub, B[8]);
  xor xor_10 (xor_10_out, Sub, B[9]);
  xor xor_11 (xor_11_out, Sub, B[10]);
  xor xor_12 (xor_12_out, Sub, B[11]);
  xor xor_13 (xor_13_out, Sub, B[12]);
  xor xor_14 (xor_14_out, Sub, B[13]);
  xor xor_15 (xor_15_out, Sub, B[14]);
  adder_16_bits adder_16_bits_1 (
    .Cin(Sub), .A0(A[0]), .B0(xor_1_out), .A1(A[1]), .B1(xor_2_out), .A2(A[2]), .B2(xor_3_out), .A3(A[3]),
    .B3(xor_4_out), .A4(A[4]), .B4(xor_5_out), .A5(A[5]), .B5(xor_6_out), .A6(A[6]), .B6(xor_7_out),
    .A7(A[7]), .B7(xor_8_out), .A8(A[8]), .B8(xor_9_out), .A9(A[9]), .B9(xor_10_out), .A10(A[10]),
    .B10(xor_11_out), .A11(A[11]), .B11(xor_12_out), .A12(A[12]), .B12(xor_13_out), .A13(A[13]),
    .B13(xor_14_out), .A14(A[14]), .B14(xor_15_out), .A15(A[15]), .B15(xor_16_out), .Cout(Cout),
    .Sum0(Sum[0]), .Sum1(Sum[1]), .Sum2(Sum[2]), .Sum3(Sum[3]), .Sum4(Sum[4]), .Sum5(Sum[5]), .Sum6(Sum[6]),
    .Sum7(Sum[7]), .Sum8(Sum[8]), .Sum9(Sum[9]), .Sum10(Sum[10]), .Sum11(Sum[11]), .Sum12(Sum[12]),
    .Sum13(Sum[13]), .Sum14(Sum[14]), .Sum15(SF));
  xor xor_16 (xor_16_out, Sub, B[15]);
  xor xor_17 (OF, Sub, Cout);
  nor nor_1 (ZF, SF, Sum[14], Sum[13], Sum[12], Sum[11], Sum[10], Sum[9], Sum[8], Sum[7], Sum[6], Sum[5], Sum[4], Sum[3], Sum[2], Sum[1], Sum[0]);

  assign Sum[15] = SF;
endmodule
