// Digital circuit adder_16_bits.dig as structural Verilog
module adder_16_bits (
  input  B3,
  input  A3,
  input  B2,
  input  A2,
  input  B1,
  input  A1,
  input  B0,
  input  A0,
  input  Cin,
  input  B7,
  input  A7,
  input  B6,
  input  A6,
  input  B5,
  input  A5,
  input  B4,
  input  A4,
  input  B11,
  input  A11,
  input  B10,
  input  A10,
  input  B9,
  input  A9,
  input  B8,
  input  A8,
  input  B15,
  input  A15,
  input  B14,
  input  A14,
  input  B13,
  input  A13,
  input  B12,
  input  A12,
  output Sum3,
  output Sum2,
  output Sum1,
  output Sum0,
  output Sum7,
  output Sum6,
  output Sum5,
  output Sum4,
  output Sum11,
  output Sum10,
  output Sum9,
  output Sum8,
  output Sum15,
  output Sum14,
  output Sum13,
  output Sum12,
  output Cout
);

  wire adder_4_bits_1_cout, adder_4_bits_2_cout, adder_4_bits_3_cout;

  adder_4_bits adder_4_bits_1 (
    .A0(A0), .B0(B0), .B1(A1), .A1(B1), .A2(A2), .B2(B2), .A3(A3), .B3(B3), .Cin(Cin), .Sum3(Sum3),
    .Sum2(Sum2), .Sum1(Sum1), .Sum0(Sum0), .Cout(adder_4_bits_1_cout));
  adder_4_bits adder_4_bits_2 (
    .A0(A4), .B0(B4), .B1(A5), .A1(B5), .A2(A6), .B2(B6), .A3(A7), .B3(B7), .Cin(adder_4_bits_1_cout),
    .Sum3(Sum7), .Sum2(Sum6), .Sum1(Sum5), .Sum0(Sum4), .Cout(adder_4_bits_2_cout));
  adder_4_bits adder_4_bits_3 (
    .A0(A8), .B0(B8), .B1(A9), .A1(B9), .A2(A10), .B2(B10), .A3(A11), .B3(B11), .Cin(adder_4_bits_2_cout),
    .Sum3(Sum11), .Sum2(Sum10), .Sum1(Sum9), .Sum0(Sum8), .Cout(adder_4_bits_3_cout));
  adder_4_bits adder_4_bits_4 (
    .A0(A12), .B0(B12), .B1(A13), .A1(B13), .A2(A14), .B2(B14), .A3(A15), .B3(B15),
    .Cin(adder_4_bits_3_cout), .Sum3(Sum15), .Sum2(Sum14), .Sum1(Sum13), .Sum0(Sum12), .Cout(Cout));
endmodule
