// Digital circuit full_adder.dig as structural Verilog
module full_adder (
  input  A,
  input  B,
  input  Cin,
  output Sum,
  output Cout
);

  wire half_adder_1_cout, half_adder_1_sum, half_adder_2_cout;

  half_adder half_adder_1 (.A(A), .B(B), .Sum(half_adder_1_sum), .Cout(half_adder_1_cout));
  half_adder half_adder_2 (.A(half_adder_1_sum), .B(Cin), .Sum(Sum), .Cout(half_adder_2_cout));
  or or_1 (Cout, half_adder_1_cout, half_adder_2_cout);
endmodule
