// Digital circuit ALU.dig as structural Verilog
module ALU (
  input  [15:0] A,
  input  [15:0] B,
  input  [2:0] ALU_Op,
  input  MDU_op,
  input  Sub,
  output [15:0] Out,
  output Flag_RZ,
  output Flag_DZ,
  output Flag_N,
  output Flag_Z,
  output OF,
  output ZF,
  output Cout,
  output [15:0] Out_HI_Rest,
  output SF
);

  wire [15:0] add_sub_16_bits_1_sum, and_1_out, mdu_1_lo, or_1_out, shift_left_16bits_1_out,
       shift_right_16bits_1_out, xor_1_out;

  add_sub_16_bits add_sub_16_bits_1 (
    .Sub(Sub), .A(A), .B(B), .Sum(add_sub_16_bits_1_sum), .Cout(Cout), .SF(SF), .ZF(ZF), .OF(OF));
  MDU mdu_1 (
    .A(A), .B(B), .MDU_op(MDU_op), .LO(mdu_1_lo), .HI(Out_HI_Rest), .Flag_Z(Flag_Z), .Flag_N(Flag_N),
    .Flag_RZ(Flag_RZ), .Flag_DZ(Flag_DZ));
  shift_left_16bits shift_left_16bits_1 (.Data_In(A), .Shamt(B[3:0]), .Out(shift_left_16bits_1_out));
  shift_right_16bits shift_right_16bits_1 (.Data_In(A), .Shamt(B[3:0]), .Out(shift_right_16bits_1_out));
  assign and_1_out = A & B;  // And and_1, 16 bits wide
  assign or_1_out = A | B;  // Or or_1, 16 bits wide
  assign xor_1_out = A ^ B;  // XOr xor_1, 16 bits wide
  Multiplexer #(.Selector_Bits(3), .Bits(16)) multiplexer_1 (
    .sel(ALU_Op), .in_0(add_sub_16_bits_1_sum), .in_1(mdu_1_lo), .in_2(shift_left_16bits_1_out),
    .in_3(shift_right_16bits_1_out), .in_4(and_1_out), .in_5(or_1_out), .in_6(xor_1_out), .in_7({16{1'b0}}),
    .out(Out));
endmodule
