// Digital circuit shift_left_16bits.dig as structural Verilog
module shift_left_16bits (
  input  [15:0] Data_In,
  input  [3:0] Shamt,
  output [15:0] Out
);

  wire [15:0] mux_2_1_16bits_2_out, mux_2_1_16bits_3_out;
  wire [15:2] mux_2_1_16bits_1_out;
  wire [15:14] mux_2_1_16bits_1_out_2;

  mux_2_1_16bits mux_2_1_16bits_1 (
    .In_0(Data_In), .In_1({Data_In[14:0], 1'b0}), .S(Shamt[0]),
    .Out({mux_2_1_16bits_1_out_2, mux_2_1_16bits_1_out}));
  mux_2_1_16bits mux_2_1_16bits_2 (
    .In_0({mux_2_1_16bits_1_out_2, mux_2_1_16bits_1_out}), .In_1({mux_2_1_16bits_1_out, 2'b00}),
    .S(Shamt[1]), .Out(mux_2_1_16bits_2_out));
  mux_2_1_16bits mux_2_1_16bits_3 (
    .In_0(mux_2_1_16bits_2_out), .In_1({mux_2_1_16bits_2_out[11:0], 4'b0000}), .S(Shamt[2]),
    .Out(mux_2_1_16bits_3_out));
  mux_2_1_16bits mux_2_1_16bits_4 (
    .In_0(mux_2_1_16bits_3_out), .In_1({mux_2_1_16bits_3_out[7:0], {8{1'b0}}}), .S(Shamt[3]), .Out(Out));
endmodule
