// Digital circuit switch_1bit.dig as structural Verilog
module switch_1bit (
  input  Data_In,
  input  Enable,
  output Out
);

  wire not_1_out;

  not not_1 (not_1_out, Enable);
  PFET pfet_1 (.G(not_1_out), .S(Data_In), .D(Out));
  NFET nfet_1 (.G(Enable), .D(Data_In), .S(Out));
endmodule
