// Digital circuit tristate_16bits.dig as structural Verilog
module tristate_16bits (
  input  [15:0] Data_In,
  input  Enable,
  output [15:0] Out
);

  switch_1bit switch_1bit_1 (.Data_In(Data_In[0]), .Enable(Enable), .Out(Out[0]));
  switch_1bit switch_1bit_2 (.Data_In(Data_In[4]), .Enable(Enable), .Out(Out[4]));
  switch_1bit switch_1bit_3 (.Data_In(Data_In[8]), .Enable(Enable), .Out(Out[8]));
  switch_1bit switch_1bit_4 (.Data_In(Data_In[12]), .Enable(Enable), .Out(Out[12]));
  switch_1bit switch_1bit_5 (.Data_In(Data_In[1]), .Enable(Enable), .Out(Out[1]));
  switch_1bit switch_1bit_6 (.Data_In(Data_In[5]), .Enable(Enable), .Out(Out[5]));
  switch_1bit switch_1bit_7 (.Data_In(Data_In[9]), .Enable(Enable), .Out(Out[9]));
  switch_1bit switch_1bit_8 (.Data_In(Data_In[13]), .Enable(Enable), .Out(Out[13]));
  switch_1bit switch_1bit_9 (.Data_In(Data_In[2]), .Enable(Enable), .Out(Out[2]));
  switch_1bit switch_1bit_10 (.Data_In(Data_In[6]), .Enable(Enable), .Out(Out[6]));
  switch_1bit switch_1bit_11 (.Data_In(Data_In[10]), .Enable(Enable), .Out(Out[10]));
  switch_1bit switch_1bit_12 (.Data_In(Data_In[14]), .Enable(Enable), .Out(Out[14]));
  switch_1bit switch_1bit_13 (.Data_In(Data_In[3]), .Enable(Enable), .Out(Out[3]));
  switch_1bit switch_1bit_14 (.Data_In(Data_In[7]), .Enable(Enable), .Out(Out[7]));
  switch_1bit switch_1bit_15 (.Data_In(Data_In[11]), .Enable(Enable), .Out(Out[11]));
  switch_1bit switch_1bit_16 (.Data_In(Data_In[15]), .Enable(Enable), .Out(Out[15]));
endmodule
