// Digital circuit CPU.dig as structural Verilog
module CPU (
  input  Reset,
  input  Clk,
  output [15:0] Out,
  output [15:0] PC_Out
);

  wire and_7_out, and_8_out, and_9_out, Cout, D0, D1, D2, D3, D4, D5, D6, D7, D8, D9, D10, D11, D12, D13,
       D14, D15, datapath_1_zf, DZ, F0, F1, F2, F3, F4, F5, F6, F7, Jump_EN, N, not_1_out, not_2_out,
       not_3_out, or_1_out, or_3_out, or_4_out, or_5_out, or_11_out, or_12_out, or_15_out, or_16_out,
       Reset_t, RZ, S1, S2, S3, S4, S5, S6, WE, Z;
  wire [0:0] or_7_out;
  wire [1:0] or_14_out;
  wire [2:0] or_9_out, register_16bits_reset_1_q_2;
  wire [3:0] Address, multiplexer_3_out, register_16bits_1_q, register_16bits_reset_1_q_3;
  wire [11:0] register_16bits_reset_1_q;
  wire [15:0] add_1_s, counter_1_out, datapath_1_regb_out, multiplexer_1_out, multiplexer_2_out,
       multiplexer_4_out, multiplexer_5_out, Out_High_Rest, ram_1_data_out, RegA, register_16bits_2_q,
       rom_1_d;
  wire [15:4] multiplexer_3_out_2, register_16bits_1_q_2;

  Decoder #(.Selector_Bits(3)) decoder_1 (
    .sel(register_16bits_reset_1_q_2), .out_0(F0), .out_1(F1), .out_2(F2), .out_3(F3), .out_4(F4),
    .out_5(F5), .out_6(F6), .out_7(F7));
  and and_1 (S1, D0, F1);
  and and_2 (S2, D0, F2);
  and and_3 (S3, D0, F3);
  and and_4 (S4, D0, F4);
  and and_5 (S5, D0, F5);
  and and_6 (S6, D0, F6);
  Counter #(.Bits(16)) counter_1 (.en(not_1_out), .C(Clk), .clr(1'b0), .out(counter_1_out));  // open: ovf
  or or_1 (or_1_out, S6, or_1_out);
  not not_1 (not_1_out, counter_1_out[2]);
  not not_2 (not_2_out, Reset_t);
  or or_2 (Reset_t, Reset, not_1_out);
  ROM #(.AddrBits(16), .Bits(16)) rom_1 (.A(PC_Out), .sel(1'b1), .D(rom_1_d));
  and and_7 (and_7_out, or_1_out, not_2_out);
  or or_3 (or_3_out, S1, S2, S3, S4, Reset_t);
  or or_4 (or_4_out, Reset_t, Jump_EN);
  register_16bits_reset register_16bits_reset_1 (
    .Reset(or_4_out), .Data_In(rom_1_d), .Clk(Clk), .EN(1'b1),
    .Q({register_16bits_reset_1_q_3, register_16bits_reset_1_q[11:9], register_16bits_reset_1_q_2, register_16bits_reset_1_q[5:0]}));
  register_16bits register_16bits_1 (
    .D({multiplexer_3_out_2, multiplexer_3_out}), .Clk(Clk), .EN(or_3_out),
    .Q({register_16bits_1_q_2, register_16bits_1_q}));
  Decoder #(.Selector_Bits(4)) decoder_2 (
    .sel(register_16bits_reset_1_q_3), .out_0(D0), .out_1(D1), .out_2(D2), .out_3(D3), .out_4(D4),
    .out_5(D5), .out_6(D6), .out_7(D7), .out_8(D8), .out_9(D9), .out_10(D10), .out_11(D11), .out_12(D12),
    .out_13(D13), .out_14(D14), .out_15(D15));
  program_counter program_counter_1 (
    .Jump_Addr(multiplexer_1_out), .Jump_EN(Jump_EN), .Reset(Reset_t), .Clk(Clk), .EN(and_7_out),
    .PC_Out(PC_Out));
  Multiplexer #(.Selector_Bits(2), .Bits(16)) multiplexer_1 (
    .sel({S3, S4}),
    .in_0({{8{1'b0}}, register_16bits_reset_1_q[11:9], register_16bits_reset_1_q_2, register_16bits_reset_1_q[5:4]}),
    .in_1(ram_1_data_out), .in_2(RegA), .in_3({16{1'b0}}), .out(multiplexer_1_out));
  Multiplexer #(.Bits(16)) multiplexer_2 (.sel(or_5_out), .in_0(16'h1), .in_1({16{1'b1}}), .out(multiplexer_2_out));
  or or_5 (or_5_out, S1, S3);
  or or_6 (WE, D15, S1, S3);
  Add #(.Bits(16)) add_1 (
    .a({register_16bits_1_q_2, register_16bits_1_q}), .b(multiplexer_2_out), .c_i(1'b0), .s(add_1_s));  // open: c_o
  datapath datapath_1 (
    .RA1(register_16bits_reset_1_q[1:0]), .RA2(register_16bits_reset_1_q[3:2]),
    .WA(register_16bits_reset_1_q[5:4]), .WE(or_11_out), .Data_In(multiplexer_5_out), .MDU_op(D4),
    .Sub(or_16_out), .ALU_Op(or_9_out), .Clk(Clk), .S(or_12_out), .Flag_RZ(RZ), .Flag_DZ(DZ), .Flag_N(N),
    .Flag_Z(Z), .ZF(datapath_1_zf), .Cout(Cout), .Out(Out), .Out_HI_Rest(Out_High_Rest), .RegA_Out(RegA),
    .RegB_Out(datapath_1_regb_out));  // open: OF, SF
  Multiplexer #(.Bits(16)) multiplexer_3 (
    .sel(Reset_t), .in_0(add_1_s), .in_1(16'hf), .out({multiplexer_3_out_2, multiplexer_3_out}));
  RAM ram_1 (.Adress(Address), .WE(WE), .Clk(Clk), .Data_In(multiplexer_4_out), .Data_Out(ram_1_data_out));
  or or_7 (or_7_out[0], D10, S2);
  or or_8 (or_9_out[0], D3, D4, D6, D8);
  or or_9 (or_9_out[1], D5, D6, D9);
  or or_10 (or_9_out[2], D7, D8, D9);
  Multiplexer #(.Bits(16)) multiplexer_4 (.sel(S3), .in_0(datapath_1_regb_out), .in_1(PC_Out), .out(multiplexer_4_out));
  Multiplexer #(.Selector_Bits(2), .Bits(16)) multiplexer_5 (
    .sel({S5, or_7_out[0]}),
    .in_0({{10{1'b0}}, register_16bits_reset_1_q[11:9], register_16bits_reset_1_q_2}), .in_1(ram_1_data_out),
    .in_2(register_16bits_2_q), .in_3({16{1'b0}}), .out(multiplexer_5_out));
  or or_11 (or_11_out, D1, D2, D3, D4, D5, D6, D7, D8, D9, D10, D11, S2, S5);
  Multiplexer #(.Selector_Bits(2), .Bits(4)) multiplexer_6 (
    .sel(or_14_out), .in_0(RegA[3:0]), .in_1(multiplexer_3_out), .in_2(register_16bits_1_q), .in_3(4'b0000),
    .out(Address));
  register_16bits register_16bits_2 (.D(Out_High_Rest), .Clk(Clk), .EN(or_15_out), .Q(register_16bits_2_q));
  or or_12 (or_12_out, D1, D2, D3, D4, D5, D6, D7, D8, D9);
  or or_13 (or_14_out[1], S2, S4);
  or or_14 (or_14_out[0], S1, S3);
  or or_15 (or_15_out, D3, D4);
  or or_16 (or_16_out, D2, D13, D14);
  not not_3 (not_3_out, datapath_1_zf);
  and and_8 (and_8_out, D14, not_3_out);
  and and_9 (and_9_out, D13, datapath_1_zf);
  or or_17 (Jump_EN, and_8_out, D12, S4, S3, and_9_out);

  // Notes on the sheet:
  //   contents of rom_1 (hex, n*v repeats v):
  //   b1c0,180,b150
endmodule
