// Digital circuit decoder_3to8.dig as structural Verilog
module decoder_3to8 (
  input  [2:0] OpCode,
  output [7:0] Control_Bus
);

  wire not_1_out, not_2_out, not_3_out;

  not not_1 (not_1_out, OpCode[0]);
  not not_2 (not_2_out, OpCode[1]);
  not not_3 (not_3_out, OpCode[2]);
  and and_1 (Control_Bus[0], not_1_out, not_2_out, not_3_out);
  and and_2 (Control_Bus[1], OpCode[0], not_2_out, not_3_out);
  and and_3 (Control_Bus[2], not_1_out, OpCode[1], not_3_out);
  and and_4 (Control_Bus[3], OpCode[0], OpCode[1], not_3_out);
  and and_5 (Control_Bus[4], not_1_out, not_2_out, OpCode[2]);
  and and_6 (Control_Bus[5], OpCode[0], not_2_out, OpCode[2]);
  and and_7 (Control_Bus[6], not_1_out, OpCode[1], OpCode[2]);
  and and_8 (Control_Bus[7], OpCode[0], OpCode[1], OpCode[2]);
endmodule
