// Digital circuit decoder_4to16bits.dig as structural Verilog
module decoder_4to16bits (
  input  [3:0] OpCode,
  output [15:0] Out
);

  wire not_1_out, not_2_out, not_3_out, not_4_out;

  not not_1 (not_1_out, OpCode[3]);
  not not_2 (not_2_out, OpCode[2]);
  not not_3 (not_3_out, OpCode[1]);
  not not_4 (not_4_out, OpCode[0]);
  and and_1 (Out[0], not_4_out, not_3_out, not_2_out, not_1_out);
  and and_2 (Out[1], OpCode[0], not_3_out, not_2_out, not_1_out);
  and and_3 (Out[2], not_4_out, OpCode[1], not_2_out, not_1_out);
  and and_4 (Out[3], OpCode[0], OpCode[1], not_2_out, not_1_out);
  and and_5 (Out[4], not_4_out, not_3_out, OpCode[2], not_1_out);
  and and_6 (Out[5], OpCode[0], not_3_out, OpCode[2], not_1_out);
  and and_7 (Out[6], not_4_out, OpCode[1], OpCode[2], not_1_out);
  and and_8 (Out[7], OpCode[0], OpCode[1], OpCode[2], not_1_out);
  and and_9 (Out[8], not_4_out, not_3_out, not_2_out, OpCode[3]);
  and and_10 (Out[9], OpCode[0], not_3_out, not_2_out, OpCode[3]);
  and and_11 (Out[10], not_4_out, OpCode[1], not_2_out, OpCode[3]);
  and and_12 (Out[11], OpCode[0], OpCode[1], not_2_out, OpCode[3]);
  and and_13 (Out[12], not_4_out, not_3_out, OpCode[2], OpCode[3]);
  and and_14 (Out[13], OpCode[0], not_3_out, OpCode[2], OpCode[3]);
  and and_15 (Out[14], not_4_out, OpCode[1], OpCode[2], OpCode[3]);
  and and_16 (Out[15], OpCode[0], OpCode[1], OpCode[2], OpCode[3]);
endmodule
