// Digital circuit nand.dig as structural Verilog
module \nand  (
  input  in_1,
  input  in_3,
  output out_2
);

  wire nfet_1_s;

  PFET pfet_1 (.G(in_1), .S(1'b1), .D(out_2));
  NFET nfet_1 (.G(in_1), .D(out_2), .S(nfet_1_s));
  NFET #(.unidirectional("true")) nfet_2 (.G(in_3), .D(nfet_1_s), .S(1'b0));
  PFET #(.unidirectional("true")) pfet_2 (.G(in_3), .S(1'b1), .D(out_2));
endmodule
