// Digital circuit nor.dig as structural Verilog
module \nor  (
  input  in_1,
  input  in_3,
  output out_2
);

  wire pfet_1_d;

  NFET nfet_1 (.G(in_1), .D(out_2), .S(1'b0));
  PFET pfet_1 (.G(in_1), .S(1'b1), .D(pfet_1_d));
  PFET #(.unidirectional("true")) pfet_2 (.G(in_3), .S(pfet_1_d), .D(out_2));
  NFET #(.unidirectional("true")) nfet_2 (.G(in_3), .D(out_2), .S(1'b0));
endmodule
