// Digital circuit not.dig as structural Verilog
module \not  (
  input  in_1,
  output out_2
);

  PFET pfet_1 (.G(in_1), .S(1'b1), .D(out_2));
  NFET nfet_1 (.G(in_1), .D(out_2), .S(1'b0));
endmodule
