// Digital circuit div_cell_16_bits.dig as structural Verilog
module div_cell_16_bits (
  input  [15:0] Rin,
  input  [15:0] Din,
  output Cout,
  output [15:0] Rout
);

  wire div_cell_8_bits_1_cout, not_1_out;

  div_cell_8_bits div_cell_8_bits_1 (
    .Rin(Rin[7:0]), .Din(Din[7:0]), .Cin(1'b1), .Restore(not_1_out), .Cout(div_cell_8_bits_1_cout),
    .Rout(Rout[7:0]));
  div_cell_8_bits div_cell_8_bits_2 (
    .Rin(Rin[15:8]), .Din(Din[15:8]), .Cin(div_cell_8_bits_1_cout), .Restore(not_1_out), .Cout(Cout),
    .Rout(Rout[15:8]));
  not not_1 (not_1_out, Cout);
endmodule
