// Digital circuit div_cell_1_bit.dig as structural Verilog
module div_cell_1_bit (
  input  Rin,
  input  Din,
  input  Cin,
  input  Restore,
  output Rout,
  output Cout
);

  wire full_adder_1_sum, not_1_out;

  not not_1 (not_1_out, Din);
  full_adder full_adder_1 (.A(Rin), .B(not_1_out), .Cin(Cin), .Sum(full_adder_1_sum), .Cout(Cout));
  mux_2_1 mux_2_1_1 (.D0(full_adder_1_sum), .D1(Rin), .S(Restore), .Out(Rout));
endmodule
