// Digital circuit div_cell_4_bits.dig as structural Verilog
module div_cell_4_bits (
  input  [3:0] Rin,
  input  [3:0] Din,
  input  Cin,
  input  Restore,
  output [3:0] Rout,
  output Cout
);

  wire div_cell_1_bit_1_cout, div_cell_1_bit_2_cout, div_cell_1_bit_3_cout;

  div_cell_1_bit div_cell_1_bit_1 (
    .Rin(Rin[0]), .Din(Din[0]), .Cin(Cin), .Restore(Restore), .Rout(Rout[0]), .Cout(div_cell_1_bit_1_cout));
  div_cell_1_bit div_cell_1_bit_2 (
    .Rin(Rin[1]), .Din(Din[1]), .Cin(div_cell_1_bit_1_cout), .Restore(Restore), .Rout(Rout[1]),
    .Cout(div_cell_1_bit_2_cout));
  div_cell_1_bit div_cell_1_bit_3 (
    .Rin(Rin[2]), .Din(Din[2]), .Cin(div_cell_1_bit_2_cout), .Restore(Restore), .Rout(Rout[2]),
    .Cout(div_cell_1_bit_3_cout));
  div_cell_1_bit div_cell_1_bit_4 (
    .Rin(Rin[3]), .Din(Din[3]), .Cin(div_cell_1_bit_3_cout), .Restore(Restore), .Rout(Rout[3]), .Cout(Cout));
endmodule
