// Digital circuit div_cell_8_bits.dig as structural Verilog
module div_cell_8_bits (
  input  [7:0] Rin,
  input  [7:0] Din,
  input  Cin,
  input  Restore,
  output Cout,
  output [7:0] Rout
);

  wire div_cell_4_bits_1_cout;

  div_cell_4_bits div_cell_4_bits_1 (
    .Rin(Rin[3:0]), .Din(Din[3:0]), .Cin(Cin), .Restore(Restore), .Rout(Rout[3:0]),
    .Cout(div_cell_4_bits_1_cout));
  div_cell_4_bits div_cell_4_bits_2 (
    .Rin(Rin[7:4]), .Din(Din[7:4]), .Cin(div_cell_4_bits_1_cout), .Restore(Restore), .Rout(Rout[7:4]),
    .Cout(Cout));
endmodule
