// Digital circuit full_divider_16_bits.dig as structural Verilog
module full_divider_16_bits (
  input  [15:0] Dividend,
  input  [15:0] Divisor,
  output [15:0] Quotient,
  output [15:0] Rest,
  output FDZ,
  output FRZ,
  output FN
);

  wire nor_1_out, nor_2_out;
  wire [15:0] div_cell_16_bits_1_rout, div_cell_16_bits_2_rout, div_cell_16_bits_3_rout,
       div_cell_16_bits_4_rout, div_cell_16_bits_5_rout, div_cell_16_bits_6_rout, div_cell_16_bits_7_rout,
       div_cell_16_bits_8_rout, div_cell_16_bits_9_rout, div_cell_16_bits_10_rout, div_cell_16_bits_11_rout,
       div_cell_16_bits_12_rout, div_cell_16_bits_13_rout, div_cell_16_bits_14_rout, div_cell_16_bits_15_rout;

  nor nor_1 (nor_1_out, Divisor[0], Divisor[1], Divisor[2], Divisor[3], Divisor[4], Divisor[5], Divisor[6], Divisor[7], Divisor[8], Divisor[9], Divisor[10], Divisor[11], Divisor[12], Divisor[13], Divisor[14], Divisor[15]);
  or or_1 (FDZ, nor_2_out, nor_1_out);
  nor nor_2 (nor_2_out, Dividend[0], Dividend[1], Dividend[2], Dividend[3], Dividend[4], Dividend[5], Dividend[6], Dividend[7], Dividend[8], Dividend[9], Dividend[10], Dividend[11], Dividend[12], Dividend[13], Dividend[14], Dividend[15]);
  div_cell_16_bits div_cell_16_bits_1 (
    .Rin({{15{1'b0}}, Dividend[15]}), .Din(Divisor), .Cout(FN), .Rout(div_cell_16_bits_1_rout));
  div_cell_16_bits div_cell_16_bits_2 (
    .Rin({div_cell_16_bits_13_rout[14:0], Dividend[11]}), .Din(Divisor), .Cout(Quotient[11]),
    .Rout(div_cell_16_bits_2_rout));
  div_cell_16_bits div_cell_16_bits_3 (
    .Rin({div_cell_16_bits_14_rout[14:0], Dividend[7]}), .Din(Divisor), .Cout(Quotient[7]),
    .Rout(div_cell_16_bits_3_rout));
  div_cell_16_bits div_cell_16_bits_4 (
    .Rin({div_cell_16_bits_15_rout[14:0], Dividend[3]}), .Din(Divisor), .Cout(Quotient[3]),
    .Rout(div_cell_16_bits_4_rout));
  div_cell_16_bits div_cell_16_bits_5 (
    .Rin({div_cell_16_bits_1_rout[14:0], Dividend[14]}), .Din(Divisor), .Cout(Quotient[14]),
    .Rout(div_cell_16_bits_5_rout));
  div_cell_16_bits div_cell_16_bits_6 (
    .Rin({div_cell_16_bits_2_rout[14:0], Dividend[10]}), .Din(Divisor), .Cout(Quotient[10]),
    .Rout(div_cell_16_bits_6_rout));
  div_cell_16_bits div_cell_16_bits_7 (
    .Rin({div_cell_16_bits_3_rout[14:0], Dividend[6]}), .Din(Divisor), .Cout(Quotient[6]),
    .Rout(div_cell_16_bits_7_rout));
  div_cell_16_bits div_cell_16_bits_8 (
    .Rin({div_cell_16_bits_4_rout[14:0], Dividend[2]}), .Din(Divisor), .Cout(Quotient[2]),
    .Rout(div_cell_16_bits_8_rout));
  div_cell_16_bits div_cell_16_bits_9 (
    .Rin({div_cell_16_bits_5_rout[14:0], Dividend[13]}), .Din(Divisor), .Cout(Quotient[13]),
    .Rout(div_cell_16_bits_9_rout));
  div_cell_16_bits div_cell_16_bits_10 (
    .Rin({div_cell_16_bits_6_rout[14:0], Dividend[9]}), .Din(Divisor), .Cout(Quotient[9]),
    .Rout(div_cell_16_bits_10_rout));
  div_cell_16_bits div_cell_16_bits_11 (
    .Rin({div_cell_16_bits_7_rout[14:0], Dividend[5]}), .Din(Divisor), .Cout(Quotient[5]),
    .Rout(div_cell_16_bits_11_rout));
  div_cell_16_bits div_cell_16_bits_12 (
    .Rin({div_cell_16_bits_8_rout[14:0], Dividend[1]}), .Din(Divisor), .Cout(Quotient[1]),
    .Rout(div_cell_16_bits_12_rout));
  div_cell_16_bits div_cell_16_bits_13 (
    .Rin({div_cell_16_bits_9_rout[14:0], Dividend[12]}), .Din(Divisor), .Cout(Quotient[12]),
    .Rout(div_cell_16_bits_13_rout));
  div_cell_16_bits div_cell_16_bits_14 (
    .Rin({div_cell_16_bits_10_rout[14:0], Dividend[8]}), .Din(Divisor), .Cout(Quotient[8]),
    .Rout(div_cell_16_bits_14_rout));
  div_cell_16_bits div_cell_16_bits_15 (
    .Rin({div_cell_16_bits_11_rout[14:0], Dividend[4]}), .Din(Divisor), .Cout(Quotient[4]),
    .Rout(div_cell_16_bits_15_rout));
  div_cell_16_bits div_cell_16_bits_16 (
    .Rin({div_cell_16_bits_12_rout[14:0], Dividend[0]}), .Din(Divisor), .Cout(Quotient[0]), .Rout(Rest));
  nor nor_3 (FRZ, Rest[0], Rest[1], Rest[2], Rest[3], Rest[4], Rest[5], Rest[6], Rest[7], Rest[8], Rest[9], Rest[10], Rest[11], Rest[12], Rest[13], Rest[14], Rest[15]);

  assign Quotient[15] = FN;
endmodule
