// Digital circuit full_multiplier_16_bits.dig as structural Verilog
module full_multiplier_16_bits (
  input  [15:0] A,
  input  [15:0] B,
  output [15:0] LO,
  output [15:0] HI,
  output ZF,
  output SF
);

  wire or_1_out, or_2_out;
  wire [15:0] mult_cell_16_bits_1_cout;
  wire [15:1] mult_cell_16_bits_2_sumout, mult_cell_16_bits_3_sumout, mult_cell_16_bits_4_sumout,
       mult_cell_16_bits_5_sumout, mult_cell_16_bits_6_sumout, mult_cell_16_bits_7_sumout,
       mult_cell_16_bits_8_sumout, mult_cell_16_bits_9_sumout, mult_cell_16_bits_10_sumout,
       mult_cell_16_bits_11_sumout, mult_cell_16_bits_12_sumout, mult_cell_16_bits_13_sumout,
       mult_cell_16_bits_14_sumout, mult_cell_16_bits_16_sumout;
  wire [15:15] mult_cell_16_bits_2_cout, mult_cell_16_bits_3_cout, mult_cell_16_bits_4_cout,
       mult_cell_16_bits_5_cout, mult_cell_16_bits_6_cout, mult_cell_16_bits_7_cout,
       mult_cell_16_bits_8_cout, mult_cell_16_bits_9_cout, mult_cell_16_bits_10_cout,
       mult_cell_16_bits_11_cout, mult_cell_16_bits_12_cout, mult_cell_16_bits_13_cout,
       mult_cell_16_bits_14_cout, mult_cell_16_bits_16_cout;

  mult_cell_16_bits mult_cell_16_bits_1 (
    .A(A), .SumIn({16{1'b0}}), .B(B[0]), .Cin(1'b0), .SumOut({mult_cell_16_bits_1_cout[14:0], LO[0]}),
    .Cout(mult_cell_16_bits_1_cout[15]));
  mult_cell_16_bits mult_cell_16_bits_2 (
    .A(A), .SumIn({mult_cell_16_bits_16_cout[15], mult_cell_16_bits_16_sumout}), .B(B[4]), .Cin(1'b0),
    .SumOut({mult_cell_16_bits_2_sumout, LO[4]}), .Cout(mult_cell_16_bits_2_cout[15]));
  mult_cell_16_bits mult_cell_16_bits_3 (
    .A(A), .SumIn({mult_cell_16_bits_13_cout[15], mult_cell_16_bits_13_sumout}), .B(B[8]), .Cin(1'b0),
    .SumOut({mult_cell_16_bits_3_sumout, LO[8]}), .Cout(mult_cell_16_bits_3_cout[15]));
  mult_cell_16_bits mult_cell_16_bits_4 (
    .A(A), .SumIn({mult_cell_16_bits_14_cout[15], mult_cell_16_bits_14_sumout}), .B(B[12]), .Cin(1'b0),
    .SumOut({mult_cell_16_bits_4_sumout, LO[12]}), .Cout(mult_cell_16_bits_4_cout[15]));
  mult_cell_16_bits mult_cell_16_bits_5 (
    .A(A), .SumIn({mult_cell_16_bits_2_cout[15], mult_cell_16_bits_2_sumout}), .B(B[5]), .Cin(1'b0),
    .SumOut({mult_cell_16_bits_5_sumout, LO[5]}), .Cout(mult_cell_16_bits_5_cout[15]));
  mult_cell_16_bits mult_cell_16_bits_6 (
    .A(A), .SumIn({mult_cell_16_bits_3_cout[15], mult_cell_16_bits_3_sumout}), .B(B[9]), .Cin(1'b0),
    .SumOut({mult_cell_16_bits_6_sumout, LO[9]}), .Cout(mult_cell_16_bits_6_cout[15]));
  mult_cell_16_bits mult_cell_16_bits_7 (
    .A(A), .SumIn({mult_cell_16_bits_4_cout[15], mult_cell_16_bits_4_sumout}), .B(B[13]), .Cin(1'b0),
    .SumOut({mult_cell_16_bits_7_sumout, LO[13]}), .Cout(mult_cell_16_bits_7_cout[15]));
  mult_cell_16_bits mult_cell_16_bits_8 (
    .A(A), .SumIn(mult_cell_16_bits_1_cout), .B(B[1]), .Cin(1'b0),
    .SumOut({mult_cell_16_bits_8_sumout, LO[1]}), .Cout(mult_cell_16_bits_8_cout[15]));
  mult_cell_16_bits mult_cell_16_bits_9 (
    .A(A), .SumIn({mult_cell_16_bits_5_cout[15], mult_cell_16_bits_5_sumout}), .B(B[6]), .Cin(1'b0),
    .SumOut({mult_cell_16_bits_9_sumout, LO[6]}), .Cout(mult_cell_16_bits_9_cout[15]));
  mult_cell_16_bits mult_cell_16_bits_10 (
    .A(A), .SumIn({mult_cell_16_bits_6_cout[15], mult_cell_16_bits_6_sumout}), .B(B[10]), .Cin(1'b0),
    .SumOut({mult_cell_16_bits_10_sumout, LO[10]}), .Cout(mult_cell_16_bits_10_cout[15]));
  mult_cell_16_bits mult_cell_16_bits_11 (
    .A(A), .SumIn({mult_cell_16_bits_7_cout[15], mult_cell_16_bits_7_sumout}), .B(B[14]), .Cin(1'b0),
    .SumOut({mult_cell_16_bits_11_sumout, LO[14]}), .Cout(mult_cell_16_bits_11_cout[15]));
  mult_cell_16_bits mult_cell_16_bits_12 (
    .A(A), .SumIn({mult_cell_16_bits_8_cout[15], mult_cell_16_bits_8_sumout}), .B(B[2]), .Cin(1'b0),
    .SumOut({mult_cell_16_bits_12_sumout, LO[2]}), .Cout(mult_cell_16_bits_12_cout[15]));
  mult_cell_16_bits mult_cell_16_bits_13 (
    .A(A), .SumIn({mult_cell_16_bits_9_cout[15], mult_cell_16_bits_9_sumout}), .B(B[7]), .Cin(1'b0),
    .SumOut({mult_cell_16_bits_13_sumout, LO[7]}), .Cout(mult_cell_16_bits_13_cout[15]));
  mult_cell_16_bits mult_cell_16_bits_14 (
    .A(A), .SumIn({mult_cell_16_bits_10_cout[15], mult_cell_16_bits_10_sumout}), .B(B[11]), .Cin(1'b0),
    .SumOut({mult_cell_16_bits_14_sumout, LO[11]}), .Cout(mult_cell_16_bits_14_cout[15]));
  mult_cell_16_bits mult_cell_16_bits_15 (
    .A(A), .SumIn({mult_cell_16_bits_11_cout[15], mult_cell_16_bits_11_sumout}), .B(B[15]), .Cin(1'b0),
    .SumOut({HI[14:0], LO[15]}), .Cout(HI[15]));
  mult_cell_16_bits mult_cell_16_bits_16 (
    .A(A), .SumIn({mult_cell_16_bits_12_cout[15], mult_cell_16_bits_12_sumout}), .B(B[3]), .Cin(1'b0),
    .SumOut({mult_cell_16_bits_16_sumout, LO[3]}), .Cout(mult_cell_16_bits_16_cout[15]));
  or or_1 (or_1_out, LO[0], LO[1], LO[2], LO[3], LO[4], LO[5], LO[6], LO[7], LO[8], LO[9], LO[10], LO[11], LO[12], LO[13], LO[14], LO[15]);
  or or_2 (or_2_out, HI[0], HI[1], HI[2], HI[3], HI[4], HI[5], HI[6], HI[7], HI[8], HI[9], HI[10], HI[11], HI[12], HI[13], HI[14], HI[15]);
  nor nor_1 (ZF, or_1_out, or_2_out);

  assign SF = HI[15];
endmodule
