// Digital circuit mdu.dig as structural Verilog
module mdu (
  input  [15:0] A,
  input  [15:0] B,
  input  MDU_op,
  output [15:0] LO,
  output [15:0] HI,
  output Flag_Z,
  output Flag_N,
  output Flag_RZ,
  output Flag_DZ
);

  wire full_divider_16_bits_1_fdz, full_divider_16_bits_1_fn, full_divider_16_bits_1_frz,
       full_multiplier_16_bits_1_sf, full_multiplier_16_bits_1_zf;
  wire [15:0] full_divider_16_bits_1_quotient, full_divider_16_bits_1_rest, full_multiplier_16_bits_1_hi,
       full_multiplier_16_bits_1_lo, mux_2_1_16_bits_1_out, mux_2_1_16_bits_2_out, mux_2_1_16_bits_3_out,
       mux_2_1_16_bits_4_out;

  mux_2_1_16_bits mux_2_1_16_bits_1 (.In_0(A), .In_1({16{1'b0}}), .S(MDU_op), .Out(mux_2_1_16_bits_1_out));
  mux_2_1_16_bits mux_2_1_16_bits_2 (.In_0(B), .In_1({16{1'b0}}), .S(MDU_op), .Out(mux_2_1_16_bits_2_out));
  mux_2_1_16_bits mux_2_1_16_bits_3 (.In_0({16{1'b0}}), .In_1(A), .S(MDU_op), .Out(mux_2_1_16_bits_3_out));
  mux_2_1_16_bits mux_2_1_16_bits_4 (.In_0({16{1'b0}}), .In_1(B), .S(MDU_op), .Out(mux_2_1_16_bits_4_out));
  full_multiplier_16_bits full_multiplier_16_bits_1 (
    .A(mux_2_1_16_bits_1_out), .B(mux_2_1_16_bits_2_out), .LO(full_multiplier_16_bits_1_lo),
    .HI(full_multiplier_16_bits_1_hi), .ZF(full_multiplier_16_bits_1_zf), .SF(full_multiplier_16_bits_1_sf));
  full_divider_16_bits full_divider_16_bits_1 (
    .Dividend(mux_2_1_16_bits_3_out), .Divisor(mux_2_1_16_bits_4_out),
    .Quotient(full_divider_16_bits_1_quotient), .Rest(full_divider_16_bits_1_rest),
    .FDZ(full_divider_16_bits_1_fdz), .FRZ(full_divider_16_bits_1_frz), .FN(full_divider_16_bits_1_fn));
  mux_2_1_16_bits mux_2_1_16_bits_5 (
    .In_0(full_multiplier_16_bits_1_lo), .In_1(full_divider_16_bits_1_quotient), .S(MDU_op), .Out(LO));
  mux_2_1_16_bits mux_2_1_16_bits_6 (
    .In_0(full_multiplier_16_bits_1_hi), .In_1(full_divider_16_bits_1_rest), .S(MDU_op), .Out(HI));
  mux_2_1 mux_2_1_1 (.D0(1'b0), .D1(full_divider_16_bits_1_fdz), .S(MDU_op), .Out(Flag_DZ));
  mux_2_1 mux_2_1_2 (.D0(full_multiplier_16_bits_1_zf), .D1(1'b0), .S(MDU_op), .Out(Flag_Z));
  mux_2_1 mux_2_1_3 (.D0(full_multiplier_16_bits_1_sf), .D1(full_divider_16_bits_1_frz), .S(MDU_op), .Out(Flag_N));
  mux_2_1 mux_2_1_4 (.D0(1'b0), .D1(full_divider_16_bits_1_fn), .S(MDU_op), .Out(Flag_RZ));
endmodule
