// Digital circuit mult_cell_16_bits.dig as structural Verilog
module mult_cell_16_bits (
  input  [15:0] A,
  input  [15:0] SumIn,
  input  B,
  input  Cin,
  output [15:0] SumOut,
  output Cout
);

  wire mult_cell_8_bits_1_cout;

  mult_cell_8_bits mult_cell_8_bits_1 (
    .A(A[7:0]), .SumIn(SumIn[7:0]), .B(B), .Cin(Cin), .SumOut(SumOut[7:0]), .Cout(mult_cell_8_bits_1_cout));
  mult_cell_8_bits mult_cell_8_bits_2 (
    .A(A[15:8]), .SumIn(SumIn[15:8]), .B(B), .Cin(mult_cell_8_bits_1_cout), .SumOut(SumOut[15:8]), .Cout(Cout));
endmodule
