// Digital circuit mult_cell_1_bit.dig as structural Verilog
module mult_cell_1_bit (
  input  A,
  input  B,
  input  SumIn,
  input  Cin,
  output SumOut,
  output Cout
);

  wire and_1_out;

  and and_1 (and_1_out, A, B);
  full_adder full_adder_1 (.A(and_1_out), .B(SumIn), .Cin(Cin), .Sum(SumOut), .Cout(Cout));
endmodule
