// Digital circuit mult_cell_8_bits.dig as structural Verilog
module mult_cell_8_bits (
  input  [7:0] A,
  input  [7:0] SumIn,
  input  B,
  input  Cin,
  output [7:0] SumOut,
  output Cout
);

  wire mult_cell_4_bits_1_cout;

  mult_cell_4_bits mult_cell_4_bits_1 (
    .A(A[3:0]), .B(B), .SumIn(SumIn[3:0]), .Cin(Cin), .SumOut(SumOut[3:0]), .Cout(mult_cell_4_bits_1_cout));
  mult_cell_4_bits mult_cell_4_bits_2 (
    .A(A[7:4]), .B(B), .SumIn(SumIn[7:4]), .Cin(mult_cell_4_bits_1_cout), .SumOut(SumOut[7:4]), .Cout(Cout));
endmodule
