// Digital circuit mult_cell_4_bits.dig as structural Verilog
module mult_cell_4_bits (
  input  [3:0] A,
  input  B,
  input  [3:0] SumIn,
  input  Cin,
  output [3:0] SumOut,
  output Cout
);

  wire mult_cell_1_bit_1_cout, mult_cell_1_bit_2_cout, mult_cell_1_bit_3_cout;

  mult_cell_1_bit mult_cell_1_bit_1 (
    .A(A[0]), .B(B), .SumIn(SumIn[0]), .Cin(Cin), .SumOut(SumOut[0]), .Cout(mult_cell_1_bit_1_cout));
  mult_cell_1_bit mult_cell_1_bit_2 (
    .A(A[1]), .B(B), .SumIn(SumIn[1]), .Cin(mult_cell_1_bit_1_cout), .SumOut(SumOut[1]),
    .Cout(mult_cell_1_bit_2_cout));
  mult_cell_1_bit mult_cell_1_bit_3 (
    .A(A[2]), .B(B), .SumIn(SumIn[2]), .Cin(mult_cell_1_bit_2_cout), .SumOut(SumOut[2]),
    .Cout(mult_cell_1_bit_3_cout));
  mult_cell_1_bit mult_cell_1_bit_4 (
    .A(A[3]), .B(B), .SumIn(SumIn[3]), .Cin(mult_cell_1_bit_3_cout), .SumOut(SumOut[3]), .Cout(Cout));
endmodule
