// Digital circuit RAM.dig as structural Verilog
module RAM (
  input  [3:0] Adress,
  input  WE,
  input  Clk,
  input  [15:0] Data_In,
  output [15:0] Data_Out
);

  wire and_1_out, and_2_out, and_3_out, and_4_out, and_5_out, and_6_out, and_7_out, and_8_out, and_9_out,
       and_10_out, and_11_out, and_12_out, and_13_out, and_14_out, and_15_out, and_16_out, decoder_1_out_0,
       decoder_1_out_1, decoder_1_out_2, decoder_1_out_3, decoder_1_out_4, decoder_1_out_5, decoder_1_out_6,
       decoder_1_out_7, decoder_1_out_8, decoder_1_out_9, decoder_1_out_10, decoder_1_out_11,
       decoder_1_out_12, decoder_1_out_13, decoder_1_out_14, decoder_1_out_15;
  wire [15:0] register_16bits_1_q, register_16bits_2_q, register_16bits_3_q, register_16bits_4_q,
       register_16bits_5_q, register_16bits_6_q, register_16bits_7_q, register_16bits_8_q,
       register_16bits_9_q, register_16bits_10_q, register_16bits_11_q, register_16bits_12_q,
       register_16bits_13_q, register_16bits_14_q, register_16bits_15_q, register_16bits_16_q;

  Decoder #(.Selector_Bits(4)) decoder_1 (
    .sel(Adress), .out_0(decoder_1_out_0), .out_1(decoder_1_out_1), .out_2(decoder_1_out_2),
    .out_3(decoder_1_out_3), .out_4(decoder_1_out_4), .out_5(decoder_1_out_5), .out_6(decoder_1_out_6),
    .out_7(decoder_1_out_7), .out_8(decoder_1_out_8), .out_9(decoder_1_out_9), .out_10(decoder_1_out_10),
    .out_11(decoder_1_out_11), .out_12(decoder_1_out_12), .out_13(decoder_1_out_13),
    .out_14(decoder_1_out_14), .out_15(decoder_1_out_15));
  and and_1 (and_1_out, decoder_1_out_0, WE);
  and and_2 (and_2_out, decoder_1_out_1, WE);
  and and_3 (and_3_out, decoder_1_out_2, WE);
  and and_4 (and_4_out, decoder_1_out_3, WE);
  and and_5 (and_5_out, decoder_1_out_4, WE);
  and and_6 (and_6_out, decoder_1_out_5, WE);
  and and_7 (and_7_out, decoder_1_out_6, WE);
  and and_8 (and_8_out, decoder_1_out_7, WE);
  and and_9 (and_9_out, decoder_1_out_8, WE);
  and and_10 (and_10_out, decoder_1_out_9, WE);
  and and_11 (and_11_out, decoder_1_out_10, WE);
  and and_12 (and_12_out, decoder_1_out_11, WE);
  and and_13 (and_13_out, decoder_1_out_12, WE);
  and and_14 (and_14_out, decoder_1_out_13, WE);
  and and_15 (and_15_out, decoder_1_out_14, WE);
  and and_16 (and_16_out, decoder_1_out_15, WE);
  register_16bits register_16bits_1 (.D(Data_In), .Clk(Clk), .EN(and_1_out), .Q(register_16bits_1_q));
  register_16bits register_16bits_2 (.D(Data_In), .Clk(Clk), .EN(and_2_out), .Q(register_16bits_2_q));
  register_16bits register_16bits_3 (.D(Data_In), .Clk(Clk), .EN(and_3_out), .Q(register_16bits_3_q));
  register_16bits register_16bits_4 (.D(Data_In), .Clk(Clk), .EN(and_4_out), .Q(register_16bits_4_q));
  register_16bits register_16bits_5 (.D(Data_In), .Clk(Clk), .EN(and_5_out), .Q(register_16bits_5_q));
  register_16bits register_16bits_6 (.D(Data_In), .Clk(Clk), .EN(and_6_out), .Q(register_16bits_6_q));
  register_16bits register_16bits_7 (.D(Data_In), .Clk(Clk), .EN(and_7_out), .Q(register_16bits_7_q));
  register_16bits register_16bits_8 (.D(Data_In), .Clk(Clk), .EN(and_8_out), .Q(register_16bits_8_q));
  register_16bits register_16bits_9 (.D(Data_In), .Clk(Clk), .EN(and_9_out), .Q(register_16bits_9_q));
  register_16bits register_16bits_10 (.D(Data_In), .Clk(Clk), .EN(and_10_out), .Q(register_16bits_10_q));
  register_16bits register_16bits_11 (.D(Data_In), .Clk(Clk), .EN(and_11_out), .Q(register_16bits_11_q));
  register_16bits register_16bits_12 (.D(Data_In), .Clk(Clk), .EN(and_12_out), .Q(register_16bits_12_q));
  register_16bits register_16bits_13 (.D(Data_In), .Clk(Clk), .EN(and_13_out), .Q(register_16bits_13_q));
  register_16bits register_16bits_14 (.D(Data_In), .Clk(Clk), .EN(and_14_out), .Q(register_16bits_14_q));
  register_16bits register_16bits_15 (.D(Data_In), .Clk(Clk), .EN(and_15_out), .Q(register_16bits_15_q));
  register_16bits register_16bits_16 (.D(Data_In), .Clk(Clk), .EN(and_16_out), .Q(register_16bits_16_q));
  tristate_16bits tristate_16bits_1 (.Data_In(register_16bits_1_q), .Enable(decoder_1_out_0), .Out(Data_Out));
  tristate_16bits tristate_16bits_2 (.Data_In(register_16bits_2_q), .Enable(decoder_1_out_1), .Out(Data_Out));
  tristate_16bits tristate_16bits_3 (.Data_In(register_16bits_3_q), .Enable(decoder_1_out_2), .Out(Data_Out));
  tristate_16bits tristate_16bits_4 (.Data_In(register_16bits_4_q), .Enable(decoder_1_out_3), .Out(Data_Out));
  tristate_16bits tristate_16bits_5 (.Data_In(register_16bits_5_q), .Enable(decoder_1_out_4), .Out(Data_Out));
  tristate_16bits tristate_16bits_6 (.Data_In(register_16bits_6_q), .Enable(decoder_1_out_5), .Out(Data_Out));
  tristate_16bits tristate_16bits_7 (.Data_In(register_16bits_7_q), .Enable(decoder_1_out_6), .Out(Data_Out));
  tristate_16bits tristate_16bits_8 (.Data_In(register_16bits_8_q), .Enable(decoder_1_out_7), .Out(Data_Out));
  tristate_16bits tristate_16bits_9 (.Data_In(register_16bits_9_q), .Enable(decoder_1_out_8), .Out(Data_Out));
  tristate_16bits tristate_16bits_10 (.Data_In(register_16bits_10_q), .Enable(decoder_1_out_9), .Out(Data_Out));
  tristate_16bits tristate_16bits_11 (.Data_In(register_16bits_11_q), .Enable(decoder_1_out_10), .Out(Data_Out));
  tristate_16bits tristate_16bits_12 (.Data_In(register_16bits_12_q), .Enable(decoder_1_out_11), .Out(Data_Out));
  tristate_16bits tristate_16bits_13 (.Data_In(register_16bits_13_q), .Enable(decoder_1_out_12), .Out(Data_Out));
  tristate_16bits tristate_16bits_14 (.Data_In(register_16bits_14_q), .Enable(decoder_1_out_13), .Out(Data_Out));
  tristate_16bits tristate_16bits_15 (.Data_In(register_16bits_15_q), .Enable(decoder_1_out_14), .Out(Data_Out));
  tristate_16bits tristate_16bits_16 (.Data_In(register_16bits_16_q), .Enable(decoder_1_out_15), .Out(Data_Out));
endmodule
