// Digital circuit ROM.dig as structural Verilog
module ROM (
  input  [1:0] Address,
  input  Sel,
  output [15:0] Data_Out
);

  wire [15:0] multiplexer_1_out;

  Multiplexer #(.Bits(16), .Selector_Bits(2)) multiplexer_1 (
    .sel(Address), .in_0(16'h1), .in_1(16'h2), .in_2(16'h3), .in_3(16'h4), .out(multiplexer_1_out));
  Multiplexer #(.Bits(16)) multiplexer_2 (.sel(Sel), .in_0(multiplexer_1_out), .in_1({16{1'b0}}), .out(Data_Out));
endmodule
