// Digital circuit mux_16_1.dig as structural Verilog
module mux_16_1 (
  input  D0,
  input  D1,
  input  D2,
  input  D3,
  input  D4,
  input  D5,
  input  D6,
  input  D7,
  input  D8,
  input  D9,
  input  D10,
  input  D11,
  input  D12,
  input  D13,
  input  D14,
  input  D15,
  input  S0,
  input  S1,
  input  S2,
  input  S3,
  output Out
);

  wire mux_8_1_1_out, mux_8_1_2_out;

  mux_8_1 mux_8_1_1 (
    .D0(D0), .D1(D1), .D2(D2), .D3(D3), .D4(D4), .D5(D5), .D6(D6), .D7(D7), .S0(S0), .S1(S1), .S2(S2),
    .Out(mux_8_1_1_out));
  mux_8_1 mux_8_1_2 (
    .D0(D8), .D1(D9), .D2(D10), .D3(D11), .D4(D12), .D5(D13), .D6(D14), .D7(D15), .S0(S0), .S1(S1), .S2(S2),
    .Out(mux_8_1_2_out));
  mux_2_1 mux_2_1_1 (.D0(S3), .D1(mux_8_1_1_out), .S(mux_8_1_2_out));  // open: Out
endmodule
