// Digital circuit mux_2_1_real.dig as structural Verilog
module mux_2_1_real (
  input  D0,
  input  D1,
  input  S,
  output out_1
);

  wire not_1_out;

  not not_1 (not_1_out, S);
  PFET pfet_1 (.G(not_1_out), .S(out_1), .D(D1));
  PFET pfet_2 (.G(S), .S(out_1), .D(D0));
  NFET nfet_1 (.G(S), .D(out_1), .S(D1));
  NFET nfet_2 (.G(not_1_out), .D(out_1), .S(D0));
endmodule
