// Digital circuit mux_4_1.dig as structural Verilog
module mux_4_1 (
  input  D0,
  input  D1,
  input  D2,
  input  D3,
  input  S0,
  input  S1,
  output Out
);

  wire mux_2_1_1_out, mux_2_1_2_out;

  mux_2_1 mux_2_1_1 (.D0(D0), .D1(D1), .S(S0), .Out(mux_2_1_1_out));
  mux_2_1 mux_2_1_2 (.D0(D2), .D1(D3), .S(S0), .Out(mux_2_1_2_out));
  mux_2_1 mux_2_1_3 (.D0(mux_2_1_1_out), .D1(mux_2_1_2_out), .S(S1), .Out(Out));
endmodule
