// Digital circuit mux_8_1.dig as structural Verilog
module mux_8_1 (
  input  D0,
  input  D1,
  input  D2,
  input  D3,
  input  D4,
  input  D5,
  input  D6,
  input  D7,
  input  S0,
  input  S1,
  input  S2,
  output out_12
);

  wire mux_4_1_1_out, mux_4_1_2_out;

  mux_4_1 mux_4_1_1 (.D0(D0), .D1(D1), .D2(D2), .D3(D3), .S0(S0), .S1(S1), .Out(mux_4_1_1_out));
  mux_4_1 mux_4_1_2 (.D0(D4), .D1(D5), .D2(D6), .D3(D7), .S0(S0), .S1(S1), .Out(mux_4_1_2_out));
  mux_2_1 mux_2_1_1 (.D0(S2), .D1(mux_4_1_1_out), .S(mux_4_1_2_out));  // open: Out
endmodule
