// Digital circuit mux_2_1_16_bits.dig as structural Verilog
module mux_2_1_16_bits (
  input  [15:0] In_0,
  input  [15:0] In_1,
  input  S,
  output [15:0] Out
);

  // mux_2_1_4_bits mux_2_1_4_bits_1: pin names not known; wires that end beside it: In_1[3:0], In_0[3:0], S, Out[3:0]
  // mux_2_1_4_bits mux_2_1_4_bits_2: pin names not known; wires that end beside it: In_1[7:4], In_0[7:4], S, Out[7:4]
  // mux_2_1_4_bits mux_2_1_4_bits_3: pin names not known; wires that end beside it: In_1[11:8], In_0[11:8], S, Out[11:8]
  // mux_2_1_4_bits mux_2_1_4_bits_4: pin names not known; wires that end beside it: In_1[15:12], In_0[15:12], S, Out[15:12]
endmodule
