// Digital circuit mux_2_1_16bits.dig as structural Verilog
module mux_2_1_16bits (
  input  [15:0] In_0,
  input  [15:0] In_1,
  input  S,
  output [15:0] Out
);

  mux_2_1_4b mux_2_1_4b_1 (.In_1(In_1[3:0]), .In_0(In_0[3:0]), .S(S), .Out(Out[3:0]));
  mux_2_1_4b mux_2_1_4b_2 (.In_1(In_1[7:4]), .In_0(In_0[7:4]), .S(S), .Out(Out[7:4]));
  mux_2_1_4b mux_2_1_4b_3 (.In_1(In_1[11:8]), .In_0(In_0[11:8]), .S(S), .Out(Out[11:8]));
  mux_2_1_4b mux_2_1_4b_4 (.In_1(In_1[15:12]), .In_0(In_0[15:12]), .S(S), .Out(Out[15:12]));
endmodule
