// Digital circuit mux_2_1_4b.dig as structural Verilog
module mux_2_1_4b (
  input  [3:0] In_1,
  input  [3:0] In_0,
  input  S,
  output [3:0] Out
);

  mux_2_1 mux_2_1_1 (.D0(In_0[0]), .D1(In_1[0]), .S(S), .Out(Out[0]));
  mux_2_1 mux_2_1_2 (.D0(In_0[1]), .D1(In_1[1]), .S(S), .Out(Out[1]));
  mux_2_1 mux_2_1_3 (.D0(In_0[2]), .D1(In_1[2]), .S(S), .Out(Out[2]));
  mux_2_1 mux_2_1_4 (.D0(In_0[3]), .D1(In_1[3]), .S(S), .Out(Out[3]));
endmodule
