// Digital circuit program_counter.dig as structural Verilog
module program_counter (
  input  [15:0] Jump_Addr,
  input  Jump_EN,
  input  Reset,
  input  Clk,
  input  EN,
  output [15:0] PC_Out
);

  wire [15:0] add_1_s, multiplexer_1_out;

  register_16bits_reset register_16bits_reset_1 (
    .Reset(Reset), .Data_In(multiplexer_1_out), .Clk(Clk), .EN(EN), .Q(PC_Out));
  Add #(.Bits(16)) add_1 (.a(PC_Out), .b(16'h1), .c_i(1'b0), .s(add_1_s));  // open: c_o
  Multiplexer #(.Bits(16)) multiplexer_1 (.sel(Jump_EN), .in_0(add_1_s), .in_1(Jump_Addr), .out(multiplexer_1_out));
endmodule
