// Digital circuit flip_flop_d.dig as structural Verilog
module flip_flop_d (
  input  D,
  input  Clk,
  output Q,
  output Q_2
);

  wire d_latch_1_q, not_1_out;

  not not_1 (not_1_out, Clk);
  d_latch d_latch_1 (.D(D), .Clk(not_1_out), .Q(d_latch_1_q));  // open: Q_2
  d_latch d_latch_2 (.D(d_latch_1_q), .Clk(Clk), .Q(Q), .Q_2(Q_2));
endmodule
