// Digital circuit register_16bits_reset.dig as structural Verilog
module register_16bits_reset (
  input  Reset,
  input  [15:0] Data_In,
  input  Clk,
  input  EN,
  output [15:0] Q
);

  wire [15:0] multiplexer_1_out;

  Multiplexer #(.Bits(16)) multiplexer_1 (.sel(Reset), .in_0(Data_In), .in_1({16{1'b0}}), .out(multiplexer_1_out));
  register_16bits register_16bits_1 (.D(multiplexer_1_out), .Clk(Clk), .EN(EN), .Q(Q));
endmodule
