// Digital circuit register_16bits.dig as structural Verilog
module register_16bits (
  input  [15:0] D,
  input  Clk,
  input  EN,
  output [15:0] Q
);

  register_4bits register_4bits_1 (.D(D[3:0]), .Clk(Clk), .EN(EN), .Q(Q[3:0]));
  register_4bits register_4bits_2 (.D(D[7:4]), .Clk(Clk), .EN(EN), .Q(Q[7:4]));
  register_4bits register_4bits_3 (.D(D[11:8]), .Clk(Clk), .EN(EN), .Q(Q[11:8]));
  register_4bits register_4bits_4 (.D(D[15:12]), .Clk(Clk), .EN(EN), .Q(Q[15:12]));
endmodule
