// Digital circuit d_latch.dig as structural Verilog
module d_latch (
  input  D,
  input  Clk,
  output Q,
  output Q_2
);

  wire and_1_out, and_2_out, not_1_out;

  not not_1 (not_1_out, D);
  and and_1 (and_1_out, Clk, not_1_out);
  and and_2 (and_2_out, Clk, D);
  latch_sr latch_sr_1 (.Set(and_2_out), .Reset(and_1_out), .Q(Q), .Q_2(Q_2));
endmodule
