// Digital circuit register_4bits.dig as structural Verilog
module register_4bits (
  input  [3:0] D,
  input  Clk,
  input  EN,
  output [3:0] Q
);

  wire [3:0] multiplexer_1_out;

  Multiplexer #(.Bits(4)) multiplexer_1 (.sel(EN), .in_0(Q), .in_1(D), .out(multiplexer_1_out));
  flip_flop_d flip_flop_d_1 (.D(multiplexer_1_out[0]), .Clk(Clk), .Q(Q[0]));  // open: Q_2
  flip_flop_d flip_flop_d_2 (.D(multiplexer_1_out[1]), .Clk(Clk), .Q(Q[1]));  // open: Q_2
  flip_flop_d flip_flop_d_3 (.D(multiplexer_1_out[2]), .Clk(Clk), .Q(Q[2]));  // open: Q_2
  flip_flop_d flip_flop_d_4 (.D(multiplexer_1_out[3]), .Clk(Clk), .Q(Q[3]));  // open: Q_2
endmodule
