// Digital circuit register_file.dig as structural Verilog
module register_file (
  input  [15:0] Data_In,
  input  Clk,
  input  WE,
  input  [1:0] WA,
  input  [1:0] RA1,
  input  [1:0] RA2,
  output [15:0] Out_A,
  output [15:0] Out_B
);

  wire demultiplexer_1_out_0, demultiplexer_1_out_1, demultiplexer_1_out_2, demultiplexer_1_out_3;
  wire [15:0] register_16bits_1_q, register_16bits_2_q, register_16bits_3_q, register_16bits_4_q;

  Demultiplexer #(.Selector_Bits(2)) demultiplexer_1 (
    .sel(WA), .in(WE), .out_0(demultiplexer_1_out_0), .out_1(demultiplexer_1_out_1),
    .out_2(demultiplexer_1_out_2), .out_3(demultiplexer_1_out_3));
  register_16bits register_16bits_1 (.D(Data_In), .Clk(Clk), .EN(demultiplexer_1_out_0), .Q(register_16bits_1_q));
  register_16bits register_16bits_2 (.D(Data_In), .Clk(Clk), .EN(demultiplexer_1_out_1), .Q(register_16bits_2_q));
  register_16bits register_16bits_3 (.D(Data_In), .Clk(Clk), .EN(demultiplexer_1_out_2), .Q(register_16bits_3_q));
  register_16bits register_16bits_4 (.D(Data_In), .Clk(Clk), .EN(demultiplexer_1_out_3), .Q(register_16bits_4_q));
  Multiplexer #(.Selector_Bits(2), .Bits(16)) multiplexer_1 (
    .sel(RA1), .in_0(register_16bits_1_q), .in_1(register_16bits_2_q), .in_2(register_16bits_3_q),
    .in_3(register_16bits_4_q), .out(Out_A));
  Multiplexer #(.Selector_Bits(2), .Bits(16)) multiplexer_2 (
    .sel(RA2), .in_0(register_16bits_1_q), .in_1(register_16bits_2_q), .in_2(register_16bits_3_q),
    .in_3(register_16bits_4_q), .out(Out_B));
endmodule
